# Fritzing sketch Ceng318Design2 (saved by Fritzing 0.9.3b)
circuit board: 6.8962cm x 3.22692cm
breadboards: 1

parts:
  Part1 = BluePill
  Willwin_MQ-2 = MQ-3 breakout

nets:
  N1: Part1.A0, Willwin_MQ-2.AO
  N2: Part1.3V31, Willwin_MQ-2.VCC
  GND3: Part1.GND3, Willwin_MQ-2.GND
  N3: Part1.B8, Willwin_MQ-2.DO

notes:
  Lucas Finiello
  Smart Home Monitor

custom parts:
  MQ-3 breakout: Alcohol sensor is capable of detecting alcohol (ethanol) particles on itself and gives the information in digital form back to us to manipulate with it. SKU:101251 • Voltage: 5V DC • Power: max 750mW • Measurement range: 0.04-4mg/L
