# Fritzing sketch SmartHomeFinal copy (saved by Fritzing 0.9.3b)
circuit board: 7.19189cm x 4.39664cm
breadboards: 1

parts:
  MQ-2 = female pin header, 4 pins [form="♀ (female)"]
  Blue_Pill = STM32F103C8T6 blue mini board
  Buzzer = female pin header, 3 pins [form="♀ (female)"]
  Programmer = female pin header, 6 pins [form="♀ (female)"]

nets (from the pcb view):
  N1: MQ-2.pin1, Blue_Pill.5V, Buzzer.pin2, Programmer.pin3
  N2: MQ-2.pin2, Blue_Pill.G, Blue_Pill.GND, Buzzer.pin3, Programmer.pin1
  N3: MQ-2.pin4, Blue_Pill.A6
  N4: Blue_Pill.A9, Programmer.pin5
  N5: Blue_Pill.A10, Programmer.pin4
  N6: Blue_Pill.A12, Buzzer.pin1
  N7: Blue_Pill.3.3V, Blue_Pill.3.3

notes:
  Lucas Finiello

custom parts:
  STM32F103C8T6 blue mini board: Generic Blue Pill microcomputer module, available from Ebay and others. CPU STM32F103C8 72Mhz Flash: 64 KB/128 KB RAM: 20KB.
